# Fritzing sketch OnderGrup AMR v1.0 (saved by Fritzing 0.9.3b)
breadboards: 2

parts:
  Raspberry_Pi_1 = Raspberry Pi 3 [part_number=RPI-3-V1.2]
  Part1 = LIDAR-Lite
  Part2 = LIDAR-Lite
  Part3 = LIDAR-Lite
  Part4 = LIDAR-Lite
  Part5 = LIDAR-Lite
  Part6 = Adafruit TCA9548A
  M1 = DC Motor  # not connected
  M2 = DC Motor  # not connected
  M3 = DC Motor  # not connected
  M4 = DC Motor  # not connected

nets:
  N1: Raspberry_Pi_1.GPIO2, Part6.INPUTSDA
  N2: Raspberry_Pi_1.GPIO3, Part6.INPUTSCL
  GND: Raspberry_Pi_1.GND, Part1.GND, Part3.GND, Part4.GND, Part6.GND
  5V: Raspberry_Pi_1.5V, Part1.5V, Part2.5V, Part2.PWR_EN, Part3.5V, Part4.5V, Part4.PWR_EN, Part5.5V, Part6.VCC
  N3: Part1.SCL, Part6.3SCL
  N4: Part1.SDA, Part6.3SDA
  N5: Part2.SCL, Part6.2SCL
  GND_2: Part2.SDA, Part2.GND, Part5.GND, Part6.2SDA
  N6: Part3.SCL, Part6.1SCL
  N7: Part3.SDA, Part6.1SDA
  N8: Part4.SCL, Part6.4SCL
  N9: Part4.SDA, Part6.4SDA
  N10: Part5.SCL, Part6.0SCL
  N11: Part5.SDA, Part6.0SDA

notes:
  i2c Multiplexer
  TCA9548A
  5x Garmin LIDAR-Lite v3

custom parts:
  LIDAR-Lite: PulsedLight LIDAR-Lite Sensor
  Adafruit TCA9548A: You just found the perfect I2C sensor, and you want to wire up two or three or more of them to your Arduino when you realize "Uh oh, this chip has a fixed I2C address, and from what I know about I2C, you cannot have two devices with the same address on the same SDA/SCL pins!" Are you out of luck? You would be, if you didn't have this ultra-cool TCA9548A 1-to-8 I2C multiplexer! Finally, a way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
