# Fritzing sketch Battery Status (saved by Fritzing 0.9.3b)
breadboards: 1

parts:
  ADC1 = MCP3008 [package=dil16]
  Raspberry_Pi1 = Raspberry Pi B+
  Battery_Power = Battery block 9V
  D1 = LTE-302 [package=lte-302]
  D2 = LTE-302 [package=lte-302]
  R1 = Resistor [tolerance=±5% resistance=330 package="1206 [SMD]"]
  R2 = Resistor [tolerance=±5% resistance=330 package="1206 [SMD]"]
  R3 = Resistor [tolerance=±5% resistance=10k package="1206 [SMD]"]
  R4 = Resistor [tolerance=±5% resistance=10k package="1206 [SMD]"]
  C1 = Capacitor [part_number=100uF package=cap-pth-small-kit]
  C2 = Capacitor [part_number=10uF package=cap-pth-small-kit]
  D3 = Rectifier Diode [part_number=BY299 package="Melf DO-213 AB [SMD]"]
  U1 = Voltage Regulator [part_number=L78S05C package=v-reg_dpack]
  Q1 = NPN-Transistor [package="TO92 [THT]"]
  R5 = Resistor [tolerance=±5% resistance=330 package=THT]
  R6 = Resistor [tolerance=±5% resistance=220 package=THT]

nets:
  N1: ADC1.CH0, R3.Pin_1, R4.Pin_1
  N2: ADC1.DGND, ADC1.AGND, Raspberry_Pi1.GND, Battery_Power.-, D1.C, D2.C, R3.Pin_0, C1.2, C2.2, Q1.E, R6.Pin_1
  N3: ADC1.CS/SHDN, Raspberry_Pi1.GPIO8
  N4: ADC1.Din, Raspberry_Pi1.GPIO10
  N5: ADC1.Dout, Raspberry_Pi1.GPIO9
  N6: ADC1.CLK, Raspberry_Pi1.GPIO11
  3V3: ADC1.VREF, ADC1.VDD, Raspberry_Pi1.3v3, Raspberry_Pi1.3V3
  N7: Raspberry_Pi1.GPIO25, R1.Pin_0
  N8: Raspberry_Pi1.GPIO24, R2.Pin_0
  N9: Raspberry_Pi1.GPIO23, R5.Pin_1
  N10: Battery_Power.+, R4.Pin_0, D3.anode
  N11: D1.A, R1.Pin_1
  N12: D2.A, R2.Pin_1
  N13: C1.1, D3.cathode, U1.IN
  N14: C2.1, U1.OUT, R6.Pin_0
  N15: U1.ADJ, Q1.C
  N16: Q1.B, R5.Pin_0

notes:
  5 Volt Çıkış
